// Logisim project 4 BIT BINARY TO DECIMAL LOGISIM.circ as structural Verilog
module _4_BIT_BINARY_TO_DECIMAL (
  input  in_1,
  input  in_2,
  input  in_3,
  input  in_4,
  output out_5,
  output out_6,
  output out_7,
  output out_8,
  output out_9,
  output out_10,
  output out_11,
  output out_12,
  output out_13,
  output out_14
);

  wire nand_1_out, nand_2_out, nand_3_out, nand_4_out, nand_5_out, nand_6_out, nand_7_out, nand_8_out,
       nand_9_out, nand_10_out, nor_1_out, nor_2_out, nor_3_out, nor_4_out, nor_5_out, nor_6_out, nor_7_out,
       not_1_out, not_2_out, not_3_out, not_4_out, not_5_out, not_6_out, not_7_out, not_8_out;

  not not_1 (not_1_out, in_1);
  not not_2 (not_2_out, in_2);
  not not_3 (not_3_out, in_3);
  not not_4 (not_4_out, in_4);
  not not_5 (not_5_out, not_1_out);
  not not_6 (not_6_out, not_2_out);
  not not_7 (not_7_out, not_3_out);
  not not_8 (not_8_out, not_4_out);
  nor nor_1 (nor_1_out, not_5_out, not_6_out);
  nor nor_2 (nor_2_out, not_1_out, not_6_out);
  nor nor_3 (nor_3_out, not_5_out, not_2_out);
  nor nor_4 (nor_4_out, not_1_out, not_2_out);
  nor nor_5 (nor_5_out, not_7_out, not_8_out);
  not nor_6 (nor_6_out, not_8_out);  // NOR_Gate
  not nor_7 (nor_7_out, not_7_out);  // NOR_Gate
  not nand_1 (nand_1_out, nor_1_out);  // NAND_Gate
  nand nand_2 (nand_2_out, nor_2_out, nor_5_out);
  nand nand_3 (nand_3_out, nor_3_out, nor_5_out);
  nand nand_4 (nand_4_out, nor_4_out, nor_5_out);
  nand nand_5 (nand_5_out, nor_1_out, nor_6_out);
  nand nand_6 (nand_6_out, nor_2_out, nor_6_out);
  nand nand_7 (nand_7_out, nor_3_out, nor_6_out);
  nand nand_8 (nand_8_out, nor_4_out, nor_6_out);
  nand nand_9 (nand_9_out, nor_1_out, nor_7_out);
  nand nand_10 (nand_10_out, nor_2_out, nor_7_out);
  not not_9 (out_5, nand_1_out);
  not not_10 (out_6, nand_2_out);
  not not_11 (out_7, nand_3_out);
  not not_12 (out_8, nand_4_out);
  not not_13 (out_9, nand_5_out);
  not not_14 (out_10, nand_6_out);
  not not_15 (out_11, nand_7_out);
  not not_16 (out_12, nand_8_out);
  not not_17 (out_13, nand_9_out);
  not not_18 (out_14, nand_10_out);
endmodule
